# Fritzing sketch PCB FRITZING BASE (saved by Fritzing 0.9.3b)
breadboards: 2

parts:
  Componente1 = Bluetooth HC-05 Macho  # not connected
  LCD1 = LCD screen
  T1 = LM35 Temperature Sensor [package="TO92 [THT]"]
  LED1 = RGB LED (com. cathode, rbg) [package="5 mm [THT]"]
  Componente2 = Arduino Mega ADK (Rev3)
  U1 = LIPO-2000mAh [package=lipo-2000]
  SG1 = Buzzer 12mm [package=buzzer-ccv]
  SG2 = Buzzer 12mm [package=buzzer-12mm-ns]
  IC1 = DS1302 [package="SO8 [SMD]"]  # not connected
  Power_plug1 = Power plug
  R1 = TRIMPOT [package=trimpot-5mm]
  R2 = Resistor [tolerance=±5% resistance=220 package="2512 [SMD]"]
  R3 = Resistor [tolerance=±5% resistance=220 package="2512 [SMD]"]
  R4 = Resistor [tolerance=±5% resistance=220 package="2512 [SMD]"]
  D1 = Diode [package=diode-hv]  # not connected
  XTAL1 = CRYSTAL - kHz [frequency="32 kHz"]  # not connected

nets:
  GND: LCD1.VSS, LCD1.RS, LCD1.R/W, LCD1.LED-, T1.GND, LED1.common_cathode, Componente2.GND, U1.-, SG1.1, SG2.2, Power_plug1.GND, R1.WIPER
  N1: LCD1.VDD, LCD1.LED+
  N2: LCD1.V0, R1.CW
  N3: LCD1.E, Componente2.D23
  N4: LCD1.DB0, Componente2.D51/MOSI
  N5: LCD1.DB1, Componente2.D49
  N6: LCD1.DB2, Componente2.D47
  N7: LCD1.DB3, Componente2.D45
  N8: LCD1.DB4, Componente2.D43
  N9: LCD1.DB5, Componente2.D41
  N10: LCD1.DB6, Componente2.D39
  N11: LCD1.DB7, Componente2.D37
  5V: T1.+Vs, Componente2.5V, SG2.1, Power_plug1.VCC, R1.CCW
  N12: T1.Vout, Componente2.A0
  N13: LED1.red_anode, R4.Pin_1
  N14: LED1.blue_anode, R3.Pin_1
  N15: LED1.green_anode, R2.Pin_1
  N16: Componente2.D10_PWM, SG1.2
  N17: Componente2.VIN, U1.+
  N18: Componente2.D5_PWM, R2.Pin_0
  N19: Componente2.D6_PWM, R3.Pin_0
  N20: Componente2.D7_PWM, R4.Pin_0
